// Logisim project processador_Bruno.circ as structural Verilog
module Add_4 (
  input  [3:0] B,
  input  [3:0] A,
  input  Vem_1,
  output Vai_1,
  output [3:0] S
);

  wire add_1_2_vai_1, add_1_3_vai_1, add_1_4_vai_1;

  Add_1 add_1_1 (.s(S[3]), .vai_1(Vai_1), .A(A[3]), .B(B[3]), .Vem_1(add_1_2_vai_1));
  Add_1 add_1_2 (.s(S[2]), .vai_1(add_1_2_vai_1), .A(A[2]), .B(B[2]), .Vem_1(add_1_3_vai_1));
  Add_1 add_1_3 (.s(S[1]), .vai_1(add_1_3_vai_1), .A(A[1]), .B(B[1]), .Vem_1(add_1_4_vai_1));
  Add_1 add_1_4 (.s(S[0]), .vai_1(add_1_4_vai_1), .A(A[0]), .B(B[0]), .Vem_1(Vem_1));
endmodule

module Add_1 (
  input  A,
  input  B,
  input  Vem_1,
  output s,
  output vai_1
);

  wire and_1_out, and_2_out, or_1_out, xor_1_out;

  xor xor_1 (xor_1_out, A, B);
  or or_1 (or_1_out, B, Vem_1);
  and and_1 (and_1_out, B, Vem_1);
  xor xor_2 (s, xor_1_out, Vem_1);
  and and_2 (and_2_out, or_1_out, A);
  or or_2 (vai_1, and_2_out, and_1_out);
endmodule

module Sub_1 (
  input  A,
  input  B,
  input  Vem_1,
  output s,
  output vai_1
);

  wire and_1_out, and_2_out, not_1_out, or_1_out, xor_1_out;

  not not_1 (not_1_out, A);
  xor xor_1 (xor_1_out, A, B);
  or or_1 (or_1_out, B, Vem_1);
  and and_1 (and_1_out, B, Vem_1);
  xor xor_2 (s, xor_1_out, Vem_1);
  and and_2 (and_2_out, or_1_out, not_1_out);
  or or_2 (vai_1, and_2_out, and_1_out);
endmodule

module Sub_4 (
  input  [3:0] B,
  input  [3:0] A,
  input  Vem_1,
  output Vai_1,
  output [3:0] S
);

  wire sub_1_2_vai_1, sub_1_3_vai_1, sub_1_4_vai_1;

  Sub_1 sub_1_1 (.A(A[3]), .B(B[3]), .Vem_1(sub_1_2_vai_1), .s(S[3]), .vai_1(Vai_1));
  Sub_1 sub_1_2 (.A(A[2]), .B(B[2]), .Vem_1(sub_1_3_vai_1), .s(S[2]), .vai_1(sub_1_2_vai_1));
  Sub_1 sub_1_3 (.A(A[1]), .B(B[1]), .Vem_1(sub_1_4_vai_1), .s(S[1]), .vai_1(sub_1_3_vai_1));
  Sub_1 sub_1_4 (.A(A[0]), .B(B[0]), .Vem_1(Vem_1), .s(S[0]), .vai_1(sub_1_4_vai_1));
endmodule

module Buffer (
  input  [3:0] B,
  input  in_2,
  output [3:0] S
);

  assign S[3] = in_2 ? B[3] : 1'bz;  // Controlled_Buffer controlled_buffer_1
  assign S[2] = in_2 ? B[2] : 1'bz;  // Controlled_Buffer controlled_buffer_2
  assign S[1] = in_2 ? B[1] : 1'bz;  // Controlled_Buffer controlled_buffer_3
  assign S[0] = in_2 ? B[0] : 1'bz;  // Controlled_Buffer controlled_buffer_4
endmodule

module Buffer_invertido (
  input  [3:0] B,
  input  in_2,
  output [3:0] S
);

  assign S[1] = in_2 ? ~B[1] : 1'bz;  // Controlled_Inverter controlled_inverter_1
  assign S[2] = in_2 ? ~B[2] : 1'bz;  // Controlled_Inverter controlled_inverter_2
  assign S[3] = in_2 ? ~B[3] : 1'bz;  // Controlled_Inverter controlled_inverter_3
  assign S[0] = in_2 ? ~B[0] : 1'bz;  // Controlled_Inverter controlled_inverter_4
endmodule

// Dec
module Decoder (
  input  [2:0] in_1,
  output S0,
  output S1,
  output S2,
  output S3,
  output S4,
  output S5,
  output S6,
  output S7
);

  wire not_1_out, not_2_out, not_3_out, not_4_out, not_5_out, not_6_out, not_7_out, not_8_out, not_9_out,
       not_10_out, not_11_out, not_12_out;

  not not_1 (not_1_out, in_1[2]);
  not not_2 (not_2_out, in_1[1]);
  not not_3 (not_3_out, in_1[0]);
  not not_4 (not_4_out, in_1[2]);
  not not_5 (not_5_out, in_1[1]);
  not not_6 (not_6_out, in_1[2]);
  not not_7 (not_7_out, in_1[0]);
  not not_8 (not_8_out, in_1[2]);
  not not_9 (not_9_out, in_1[1]);
  not not_10 (not_10_out, in_1[0]);
  not not_11 (not_11_out, in_1[1]);
  not not_12 (not_12_out, in_1[0]);
  and and_1 (S0, not_1_out, not_2_out, not_3_out);
  and and_2 (S1, not_4_out, not_5_out, in_1[0]);
  and and_3 (S2, not_6_out, in_1[1], not_7_out);
  and and_4 (S3, not_8_out, in_1[1], in_1[0]);
  and and_5 (S4, in_1[2], not_9_out, not_10_out);
  and and_6 (S5, in_1[2], not_11_out, in_1[0]);
  and and_7 (S6, in_1[2], in_1[1], not_12_out);
  and and_8 (S7, in_1[2], in_1[1], in_1[0]);
endmodule

module Rot_L (
  input  [3:0] ABCD,
  input  [1:0] XY,
  output [3:0] abcd_2
);

  wire and_1_out, and_2_out, and_3_out, and_4_out, and_5_out, and_6_out, and_7_out, and_8_out, and_9_out;

  and and_1 (and_1_out, ~XY[1], ~XY[0], ABCD[3]);  // AND_Gate
  and and_2 (and_2_out, ~XY[1], XY[0], ABCD[2]);  // AND_Gate
  and and_3 (and_3_out, XY[1], ~XY[0], ABCD[1]);  // AND_Gate
  and and_4 (and_4_out, XY[1], XY[0], ABCD[0]);
  and and_5 (and_5_out, ~XY[1], ~XY[0], ABCD[2]);  // AND_Gate
  and and_6 (and_6_out, ~XY[1], XY[0], ABCD[1]);  // AND_Gate
  and and_7 (and_7_out, XY[1], ~XY[0], ABCD[0]);  // AND_Gate
  and and_8 (and_8_out, ~XY[1], ~XY[0], ABCD[1]);  // AND_Gate
  and and_9 (and_9_out, ~XY[1], XY[0], ABCD[0]);  // AND_Gate
  and and_10 (abcd_2[0], ~XY[1], ~XY[0], ABCD[0]);  // AND_Gate
  or or_1 (abcd_2[3], and_1_out, and_2_out, and_3_out, and_4_out);
  or or_2 (abcd_2[2], and_5_out, and_6_out, and_7_out);
  or or_3 (abcd_2[1], and_8_out, and_9_out);
endmodule

module Rot_r (
  input  [3:0] ABCD,
  input  [1:0] XY,
  output [3:0] abcd_2
);

  wire and_1_out, and_2_out, and_3_out, and_4_out, and_5_out, and_6_out, and_7_out, and_8_out, and_9_out;

  and and_1 (and_1_out, ~XY[1], ~XY[0], ABCD[0]);  // AND_Gate
  and and_2 (and_2_out, ~XY[1], XY[0], ABCD[1]);  // AND_Gate
  and and_3 (and_3_out, XY[1], ~XY[0], ABCD[2]);  // AND_Gate
  and and_4 (and_4_out, XY[1], XY[0], ABCD[3]);
  and and_5 (and_5_out, ~XY[1], ~XY[0], ABCD[1]);  // AND_Gate
  and and_6 (and_6_out, ~XY[1], XY[0], ABCD[2]);  // AND_Gate
  and and_7 (and_7_out, XY[1], ~XY[0], ABCD[3]);  // AND_Gate
  and and_8 (and_8_out, ~XY[1], ~XY[0], ABCD[2]);  // AND_Gate
  and and_9 (and_9_out, ~XY[1], XY[0], ABCD[3]);  // AND_Gate
  and and_10 (abcd_2[3], ~XY[1], ~XY[0], ABCD[3]);  // AND_Gate
  or or_1 (abcd_2[0], and_1_out, and_2_out, and_3_out, and_4_out);
  or or_2 (abcd_2[1], and_5_out, and_6_out, and_7_out);
  or or_3 (abcd_2[2], and_8_out, and_9_out);
endmodule

module or_4_bits (
  input  [3:0] B,
  input  [3:0] A,
  output [3:0] S
);

  or or_1 (S[3], A[3], B[3]);
  or or_2 (S[1], A[1], B[1]);
  or or_3 (S[2], A[2], B[2]);
  or or_4 (S[0], A[0], B[0]);
endmodule

module ALU (
  input  [3:0] A,
  input  [3:0] B,
  input  [2:0] Controle,
  output overflow,
  output overflow_2,
  output [3:0] out_6
);

  wire decoder_1_s0, decoder_1_s1, decoder_1_s2, decoder_1_s4, decoder_1_s5;
  wire [3:0] add_4_1_s, rot_l_1_abcd_2, sub_4_1_s;

  Decoder decoder_1 (
    .in_1(Controle), .S0(decoder_1_s0), .S1(decoder_1_s1), .S2(decoder_1_s2), .S4(decoder_1_s4),
    .S5(decoder_1_s5));  // open: S3, S6, S7
  Buffer buffer_1 (.in_2(decoder_1_s0), .B(B), .S(out_6));
  Add_4 add_4_1 (.A(B), .Vai_1(overflow_2), .B(A), .Vem_1(1'b0), .S(add_4_1_s));
  Buffer buffer_2 (.in_2(decoder_1_s1), .B(add_4_1_s), .S(out_6));
  Sub_4 sub_4_1 (.A(A), .B(B), .Vem_1(1'b0), .Vai_1(overflow), .S(sub_4_1_s));
  Buffer buffer_3 (.in_2(decoder_1_s2), .B(sub_4_1_s), .S(out_6));
  Buffer_invertido buffer_invertido_1 (.B(B), .in_2(decoder_1_s4), .S(out_6));
  Rot_L rot_l_1 (.abcd_2(rot_l_1_abcd_2), .ABCD(A), .XY(B[1:0]));
  Buffer buffer_4 (.in_2(decoder_1_s5), .B(rot_l_1_abcd_2), .S(out_6));
endmodule

module ULA (
  input  D,
  input  [3:0] A,
  input  [3:0] B,
  input  [2:0] Controle,
  output overflow,
  output overflow_2,
  output [3:0] out_7
);

  wire decoder_1_s0, decoder_1_s1, decoder_1_s2, decoder_1_s3, decoder_1_s4, decoder_1_s5, not_1_out;
  wire [3:0] add_4_1_s, buffer_5_s, or_4_bits_1_s, rot_l_1_abcd_2, rot_r_1_abcd_2, sub_4_1_s;

  Decoder decoder_1 (
    .in_1(Controle), .S0(decoder_1_s0), .S1(decoder_1_s1), .S2(decoder_1_s2), .S3(decoder_1_s3),
    .S4(decoder_1_s4), .S5(decoder_1_s5));  // open: S6, S7
  Buffer buffer_1 (.in_2(decoder_1_s0), .B(B), .S(out_7));
  Add_4 add_4_1 (.A(B), .Vai_1(overflow_2), .B(A), .Vem_1(1'b0), .S(add_4_1_s));
  Buffer buffer_2 (.in_2(decoder_1_s1), .B(add_4_1_s), .S(out_7));
  Sub_4 sub_4_1 (.A(A), .B(B), .Vem_1(1'b0), .Vai_1(overflow), .S(sub_4_1_s));
  Buffer buffer_3 (.in_2(decoder_1_s2), .B(sub_4_1_s), .S(out_7));
  or_4_bits or_4_bits_1 (.B(B), .S(or_4_bits_1_s), .A(A));
  Buffer buffer_4 (.in_2(decoder_1_s3), .B(or_4_bits_1_s), .S(out_7));
  Buffer_invertido buffer_invertido_1 (.B(B), .in_2(decoder_1_s4), .S(out_7));
  Rot_r rot_r_1 (.abcd_2(rot_r_1_abcd_2), .ABCD(A), .XY(B[1:0]));
  Rot_L rot_l_1 (.abcd_2(rot_l_1_abcd_2), .ABCD(A), .XY(B[1:0]));
  not not_1 (not_1_out, D);
  Buffer buffer_5 (.in_2(D), .B(rot_r_1_abcd_2), .S(buffer_5_s));
  Buffer buffer_6 (.in_2(not_1_out), .B(rot_l_1_abcd_2), .S(buffer_5_s));
  Buffer buffer_7 (.in_2(decoder_1_s5), .B(buffer_5_s), .S(out_7));
endmodule
